// Logisim project second.circ as structural Verilog: 1 circuit, main circuit main
module main (
  input  X3,
  input  X2,
  input  X1,
  input  X0,
  input  in_5,
  input  in_6,
  input  in_7,
  input  in_8,
  input  in_9,
  input  in_10,
  input  in_11,
  input  in_12,
  input  in_13,
  output T3,
  output T2,
  output T1,
  output T0,
  output P3,
  output P2,
  output P1,
  output P0,
  output U3,
  output U2,
  output U1,
  output U0,
  output M3,
  output M2,
  output M1,
  output M0
);

  not not_1 (T0, X3);
  Adder #(.width(4)) adder_1 (
    .a({X3, X2, X1, X0}), .b({in_6, in_7, in_8, in_9}), .out({P3, P2, P1, P0}));  // open: cin, cout
  Adder #(.width(4)) adder_2 (
    .a({X3, X2, X1, X0}), .b({in_10, in_11, in_12, in_13}), .out({M3, M2, M1, M0}));  // open: cin, cout
  Multiplexer #(.width(4)) multiplexer_1 (
    .in0({P3, P2, P1, P0}), .in1({M3, M2, M1, M0}), .out({U3, U2, U1, U0}), .sel(X3));  // open: en

  assign T1 = T0;
  assign T2 = X3;
  assign T3 = in_5;
endmodule
