// Logisim project third.circ as structural Verilog: 1 circuit, main circuit main
module main (
  input  Q0,
  input  Q1,
  input  CLK,
  input  T0,
  input  Q0_2,
  input  Q2,
  input  Q1_2,
  input  Q0_3,
  input  T0_2,
  output T1,
  output Q0_4,
  output T2,
  output Q1_3,
  output T2_2,
  output Q2_2,
  output Q3,
  output T3,
  output Q3_2,
  output Q2_3,
  output Q1_4,
  output Q0_5,
  output Q1_5,
  output T2_3,
  output Q0_6,
  output Q0_7,
  output Q0_8,
  output T1_2,
  output Q1_6,
  output T3_2,
  output Q0_9
);

  wire and_6_out, and_7_out, not_2_out, not_3_out, not_4_out, not_5_out, not_6_out, not_7_out, not_8_out,
       not_9_out, not_10_out, not_11_out, not_12_out, not_13_out, not_15_out, not_16_out, not_17_out,
       not_18_out, not_19_out, not_20_out;

  T_Flip_Flop t_ff_1 (.Q(Q1_5));  // open: clk, T, Qn, preset, reset, en
  T_Flip_Flop t_ff_2 (.Q(Q0_6));  // open: clk, T, Qn, preset, reset, en
  T_Flip_Flop t_ff_3 (.Q(Q0_7));  // open: clk, T, Qn, preset, reset, en
  T_Flip_Flop t_ff_4 (.Q(Q1_6));  // open: clk, T, Qn, preset, reset, en
  T_Flip_Flop t_ff_5 (.Q(Q0_9));  // open: clk, T, Qn, preset, reset, en
  not not_1 (T1, Q0);
  not not_2 (not_2_out, Q1);
  not not_3 (not_3_out, Q0_2);
  not not_4 (not_4_out, Q2);
  not not_5 (not_5_out, Q1_2);
  not not_6 (not_6_out, Q0_3);
  and and_1 (T2_2, not_2_out, not_3_out);
  and and_2 (T3, not_4_out, not_5_out, not_6_out);
  not not_7 (not_7_out, Q1_5);
  not not_8 (not_8_out, Q0_6);
  not not_9 (not_9_out, Q0_7);
  not not_10 (not_10_out, Q1_6);
  not not_11 (not_11_out, Q0_9);
  and and_3 (T2_3, not_7_out, not_8_out);
  and and_4 (T3_2, not_9_out, not_10_out, not_11_out);
  T_Flip_Flop t_ff_6 (.Q(Q0_4));  // open: clk, T, Qn, preset, reset, en
  T_Flip_Flop t_ff_7 (.Q(Q1_3));  // open: clk, T, Qn, preset, reset, en
  T_Flip_Flop t_ff_8 (.Q(Q2_2));  // open: clk, T, Qn, preset, reset, en
  T_Flip_Flop t_ff_9 (.Q(Q3));  // open: clk, T, Qn, preset, reset, en
  T_Flip_Flop t_ff_10 (.Q(Q0_8));  // open: clk, T, Qn, preset, reset, en
  not not_12 (not_12_out, Q0_4);
  not not_13 (not_13_out, Q1_3);
  not not_14 (T1_2, Q0_8);
  and and_5 (T2, not_12_out, not_13_out);
  not not_15 (not_15_out, Q0_5);
  not not_16 (not_16_out, Q1_4);
  not not_17 (not_17_out, Q0_5);
  not not_18 (not_18_out, Q2_3);
  not not_19 (not_19_out, Q1_4);
  not not_20 (not_20_out, Q0_5);
  and and_6 (and_6_out, not_16_out, not_17_out);
  and and_7 (and_7_out, not_18_out, not_19_out, not_20_out);
  T_Flip_Flop t_ff_11 (.clk(CLK), .T(T0), .Q(Q0_5));  // open: Qn, preset, reset, en
  T_Flip_Flop t_ff_12 (.clk(CLK), .T(not_15_out), .Q(Q1_4));  // open: Qn, preset, reset, en
  T_Flip_Flop t_ff_13 (.clk(CLK), .T(and_6_out), .Q(Q2_3));  // open: Qn, preset, reset, en
  T_Flip_Flop t_ff_14 (.clk(CLK), .T(and_7_out), .Q(Q3_2));  // open: Qn, preset, reset, en
endmodule
